// Digital circuit ControlUnit.dig as structural Verilog
module ControlUnit (
  input  [5:0] inst,
  input  clk,
  input  [31:0] A,
  input  [31:0] B,
  output [3:0] alu,
  output Asource,
  output [1:0] wSource,
  output load,
  output jmp,
  output call,
  output fRet,
  output ramWE,
  output ramRead,
  output GPIOIn,
  output GPIOOut
);

  wire and_1_out, and_2_out, and_3_out, and_4_out, and_5_out, and_6_out, comparator_2_eq, comparator_3_eq,
       comparator_4_eq, comparator_5_eq, comparator_6_eq, comparator_8_eq, comparator_9_eq, not_1_out,
       or_1_out, or_2_out, or_3_out;
  wire [2:0] comparator_1_gt, register_1_q;
  wire [3:0] demultiplexer_1_out_2, demultiplexer_1_out_3;

  Comparator #(.Bits(32)) comparator_1 (
    .a(A), .b(B), .gt(comparator_1_gt[0]), .eq(comparator_1_gt[1]), .lt(comparator_1_gt[2]));
  Demultiplexer #(.Selector_Bits(2), .Bits(4)) demultiplexer_1 (
    .sel(inst[5:4]), .in(inst[3:0]), .out_0(alu), .out_2(demultiplexer_1_out_2), .out_3(demultiplexer_1_out_3));  // open: out_1
  Register #(.Bits(3)) register_1 (.D(comparator_1_gt), .C(clk), .en(comparator_2_eq), .Q(register_1_q));
  Comparator #(.Bits(4)) comparator_2 (.a(demultiplexer_1_out_3), .b(4'b0001), .eq(comparator_2_eq));  // open: gt, lt
  Comparator #(.Bits(4)) comparator_3 (.a(demultiplexer_1_out_3), .b(4'b0010), .eq(comparator_3_eq));  // open: gt, lt
  Comparator #(.Bits(4)) comparator_4 (.a(demultiplexer_1_out_3), .b(4'b0011), .eq(comparator_4_eq));  // open: gt, lt
  Comparator #(.Bits(4)) comparator_5 (.a(demultiplexer_1_out_3), .b(4'b0100), .eq(comparator_5_eq));  // open: gt, lt
  Comparator #(.Bits(4)) comparator_6 (.a(demultiplexer_1_out_3), .b(4'b0101), .eq(comparator_6_eq));  // open: gt, lt
  Comparator #(.Bits(4)) comparator_7 (.a(demultiplexer_1_out_3), .b(4'b0110), .eq(jmp));  // open: gt, lt
  Comparator #(.Bits(4)) comparator_8 (.a(demultiplexer_1_out_3), .b(4'b0111), .eq(comparator_8_eq));  // open: gt, lt
  Comparator #(.Bits(4)) comparator_9 (.a(demultiplexer_1_out_3), .b(4'b1000), .eq(comparator_9_eq));  // open: gt, lt
  Comparator #(.Bits(4)) comparator_10 (.a(demultiplexer_1_out_2), .b(4'b1011), .eq(wSource[0]));  // open: gt, lt
  Comparator #(.Bits(4)) comparator_11 (.a(demultiplexer_1_out_2), .b(4'b1010), .eq(Asource));  // open: gt, lt
  Comparator #(.Bits(4)) comparator_12 (.a(demultiplexer_1_out_2), .b(4'b1000), .eq(ramWE));  // open: gt, lt
  not not_1 (not_1_out, register_1_q[1]);
  Comparator #(.Bits(4)) comparator_13 (.a(demultiplexer_1_out_2), .b(4'b1001), .eq(ramRead));  // open: gt, lt
  and and_1 (and_1_out, register_1_q[2], comparator_3_eq);
  and and_2 (and_2_out, not_1_out, comparator_6_eq);
  and and_3 (and_3_out, register_1_q[1], comparator_4_eq);
  and and_4 (and_4_out, register_1_q[0], comparator_5_eq);
  or or_1 (or_1_out, register_1_q[0], register_1_q[1]);
  or or_2 (or_2_out, register_1_q[1], register_1_q[2]);
  Comparator #(.Bits(4)) comparator_14 (.a(demultiplexer_1_out_2), .b(4'b1100), .eq(GPIOIn));  // open: gt, lt
  or or_3 (or_3_out, and_1_out, and_2_out, and_3_out, and_4_out);
  Comparator #(.Bits(4)) comparator_15 (.a(demultiplexer_1_out_2), .b(4'b1101), .eq(GPIOOut));  // open: gt, lt
  and and_5 (and_5_out, or_1_out, comparator_9_eq);
  and and_6 (and_6_out, or_2_out, comparator_8_eq);
  Comparator #(.Bits(4)) comparator_16 (.a(demultiplexer_1_out_2), .b(4'b1110), .eq(call));  // open: gt, lt
  Comparator #(.Bits(4)) comparator_17 (.a(demultiplexer_1_out_2), .b(4'b1111), .eq(fRet));  // open: gt, lt
  or or_4 (load, and_5_out, and_6_out, or_3_out);

  assign wSource[1] = Asource;

  // Notes on the sheet:
  //   disable writing to reg when op is 000000
endmodule
