// Digital circuit ScopeStack.dig as structural Verilog
module ScopeStack (
  input  [23:0] cAd,
  input  [23:0] curAd,
  input  call,
  input  fRet,
  input  clear,
  output sovf,
  output lAd,
  output [23:0] add
);

  wire or_1_out;
  wire [3:0] counterpreset_1_out;
  wire [23:0] add_1_s, registerfile_1_da;

  PullDown #(.Bits(24)) pulldown_1 (.out(cAd));
  Add #(.Bits(24)) add_1 (.a(curAd), .b(24'h1), .c_i(1'b0), .s(add_1_s));  // open: c_o
  or or_1 (or_1_out, call, fRet);
  CounterPreset #(.Bits(4)) counterpreset_1 (
    .en(1'b1), .C(or_1_out), .dir(fRet), .in(4'b0000), .ld(1'b0), .clr(clear), .out(counterpreset_1_out),
    .ovf(sovf));
  PullDown #(.Bits(24)) pulldown_2 (.out(add_1_s));
  RegisterFile #(.AddrBits(4), .Bits(24)) registerfile_1 (
    .Din(add_1_s), .we(call), .Rw(counterpreset_1_out), .C(or_1_out), .Ra(counterpreset_1_out), .Rb(4'b0000),
    .Da(registerfile_1_da));  // open: Db
  Multiplexer #(.Bits(24)) multiplexer_1 (.sel(call), .in_0(registerfile_1_da), .in_1(cAd), .out(add));
  or or_2 (lAd, call, fRet);
  PullDown #(.Bits(24)) pulldown_3 (.out(add));
endmodule
