// Digital circuit alu.dig as structural Verilog
module alu (
  input  [31:0] A,
  input  [31:0] B,
  input  [3:0] OP,
  output [31:0] out,
  output overflow
);

  wire add_1_c_o, sub_1_c_o;
  wire [0:0] comparator_1_eq, comparator_1_gt, comparator_1_lt, not_1_out;
  wire [31:0] add_1_s, and_1_out, div_1_q, div_1_r, LEFT_out, mul_1_mul, or_1_out, RIGHT_out, sub_1_s,
       xor_1_out;

  PullDown #(.Bits(32)) pulldown_1 (.out(A));
  PullDown #(.Bits(32)) pulldown_2 (.out(B));
  PullDown #(.Bits(4)) pulldown_3 (.out(OP));
  Sub #(.Bits(32)) sub_1 (.a(A), .b(B), .c_i(1'b0), .s(sub_1_s), .c_o(sub_1_c_o));
  Div #(.Bits(32)) div_1 (.a(A), .b(B), .q(div_1_q), .r(div_1_r));
  Comparator #(.Bits(32)) comparator_1 (
    .a(A), .b(B), .gt(comparator_1_gt[0]), .eq(comparator_1_eq[0]), .lt(comparator_1_lt[0]));
  assign and_1_out = A & B;  // And and_1, 32 bits wide
  assign or_1_out = A | B;  // Or or_1, 32 bits wide
  assign xor_1_out = A ^ B;  // XOr xor_1, 32 bits wide
  Add #(.Bits(32)) add_1 (.a(A), .b(B), .c_i(1'b0), .s(add_1_s), .c_o(add_1_c_o));
  Mul #(.Bits(16)) mul_1 (.a(A[15:0]), .b(B[15:0]), .mul(mul_1_mul));
  BarrelShifter #(.Bits(32)) LEFT (.in(A), .shift(B[5:0]), .out(LEFT_out));
  BarrelShifter #(.Bits(32), .direction("right")) RIGHT (.in(A), .shift(B[5:0]), .out(RIGHT_out));
  not not_1 (not_1_out[0], comparator_1_eq[0]);
  Multiplexer #(.Bits(32), .Selector_Bits(4)) multiplexer_1 (
    .sel(OP), .in_0(A), .in_1(add_1_s), .in_2(sub_1_s), .in_3(mul_1_mul), .in_4(div_1_q),
    .in_5({{31{1'b0}}, comparator_1_gt[0]}), .in_6({{31{1'b0}}, comparator_1_eq[0]}),
    .in_7({{31{1'b0}}, comparator_1_lt[0]}), .in_8({{31{1'b0}}, not_1_out[0]}), .in_9(and_1_out),
    .in_10(or_1_out), .in_11(xor_1_out), .in_12(LEFT_out), .in_13(RIGHT_out), .in_14(div_1_r),
    .in_15({32{1'b0}}), .out(out));
  or or_2 (overflow, sub_1_c_o, add_1_c_o);
endmodule
