// Digital circuit decoder.dig as structural Verilog
module decoder (
  input  [31:0] inst,
  output [15:0] \const ,
  output [5:0] OP,
  output [4:0] DEST,
  output [4:0] SRC1,
  output [4:0] SRC2
);


  assign \const  = inst[15:0];
  assign DEST = inst[25:21];
  assign OP = inst[31:26];
  assign SRC1 = inst[20:16];
  assign SRC2 = inst[20:16];
endmodule
