// Digital circuit dustcat-III.dig as structural Verilog
module dustcat_III (
  input  clk,
  input  [31:0] GPIN,
  output [23:0] program_addr,
  output [31:0] GPOUT1,
  output [31:0] GPOUT2
);

  wire controlunit_1_p5, controlunit_1_p8, controlunit_1_p9, controlunit_1_p10, controlunit_1_p13,
       controlunit_1_p14, controlunit_1_p15, decoder_1_p3, program_reset_out, pulldown_1_out, pulldown_4_out;
  wire [1:0] controlunit_1_p7, controlunit_1_p11, or_2_out;
  wire [3:0] controlunit_1_p6;
  wire [4:0] decoder_1_p4, decoder_1_p5, decoder_1_p6, multiplexer_2_out;
  wire [15:0] alu_1_out, decoder_1_p2;
  wire [23:0] controlunit_1_p3, pulldown_2_out, scopestack_1_add;
  wire [31:0] controlunit_1_p4, eepromdualport_1_d, multiplexer_3_out, multiplexer_4_out, ramdualaccess_1_d1;
  wire [31:16] alu_1_out_2;
  wire [31:24] controlunit_1_p3_2;

  Button program_reset (.out(program_reset_out));
  PullDown pulldown_1 (.out(pulldown_1_out));
  or or_1 (pulldown_1_out, or_2_out[1], controlunit_1_p14, controlunit_1_p15);
  PullDown #(.Bits(24)) pulldown_2 (.out(pulldown_2_out));
  CounterPreset #(.Bits(24)) counterpreset_1 (
    .en(1'b1), .C(clk), .dir(1'b0), .in(pulldown_2_out), .ld(pulldown_1_out), .clr(program_reset_out),
    .out(program_addr));  // open: ovf
  Multiplexer #(.Selector_Bits(2), .Bits(24)) multiplexer_1 (
    .sel(or_2_out), .in_0({24{1'b0}}), .in_1(controlunit_1_p3), .in_2(scopestack_1_add), .in_3({24{1'b0}}),
    .out(pulldown_2_out));
  or or_2 (or_2_out[0], controlunit_1_p14, controlunit_1_p15);
  EEPROMDualPort #(.AddrBits(24), .isProgramMemory("true"), .Bits(32)) eepromdualport_1 (
    .A(program_addr), .Din({32{1'b0}}), .str(1'b0), .C(clk), .ld(1'b1), .D(eepromdualport_1_d));
  // decoder decoder_1: pin names not known; wires that end beside it: eepromdualport_1_d, decoder_1_p2, decoder_1_p3, decoder_1_p4, decoder_1_p5, decoder_1_p6
  Multiplexer #(.Bits(5)) multiplexer_2 (
    .sel(controlunit_1_p5), .in_0(decoder_1_p5), .in_1(decoder_1_p4), .out(multiplexer_2_out));
  // ControlUnit controlunit_1: pin names not known; wires that end beside it: decoder_1_p3, clk, {controlunit_1_p3_2, controlunit_1_p3}, controlunit_1_p4, controlunit_1_p5, controlunit_1_p6, controlunit_1_p7, controlunit_1_p8, controlunit_1_p9, controlunit_1_p10, controlunit_1_p11[0], controlunit_1_p11[1], controlunit_1_p13, controlunit_1_p14, controlunit_1_p15
  RegisterFile #(.AddrBits(5), .Bits(32)) registerfile_1 (
    .Din(multiplexer_4_out), .we(1'b1), .Rw(decoder_1_p4), .C(clk), .Ra(multiplexer_2_out),
    .Rb(decoder_1_p6), .Da({controlunit_1_p3_2, controlunit_1_p3}), .Db(controlunit_1_p4));
  VGA vga_1 ();  // open: R, G, B, H, V, C
  alu alu_1 (
    .A({controlunit_1_p3_2, controlunit_1_p3}), .B(controlunit_1_p4), .OP(controlunit_1_p6),
    .out({alu_1_out_2, alu_1_out}));  // open: overflow
  ScopeStack scopestack_1 (
    .cAd(controlunit_1_p3), .curAd(program_addr), .call(controlunit_1_p8), .fRet(controlunit_1_p9),
    .clear(program_reset_out), .lAd(or_2_out[1]), .add(scopestack_1_add));  // open: sovf
  Multiplexer #(.Selector_Bits(2), .Bits(32)) multiplexer_3 (
    .sel(controlunit_1_p7), .in_0({alu_1_out_2, alu_1_out}), .in_1({{16{1'b0}}, decoder_1_p2}),
    .in_2({decoder_1_p2, alu_1_out}), .in_3({alu_1_out_2, alu_1_out}), .out(multiplexer_3_out));
  Multiplexer #(.Selector_Bits(2), .Bits(32)) multiplexer_4 (
    .sel(controlunit_1_p11), .in_0(multiplexer_3_out), .in_1(ramdualaccess_1_d1), .in_2(GPIN),
    .in_3({32{1'b0}}), .out(multiplexer_4_out));
  RAMDualAccess #(.AddrBits(24), .Bits(32)) ramdualaccess_1 (
    .str(controlunit_1_p10), .C(clk), .ld(controlunit_1_p11[0]), .A1(controlunit_1_p3),
    .Din1(controlunit_1_p4), .A2(24'h1), .D1(ramdualaccess_1_d1));  // open: D2
  assign GPOUT2 = controlunit_1_p13 ? controlunit_1_p4 : 32'bz;  // Driver driver_1
  PullDown pulldown_3 (.out(controlunit_1_p13));
  assign GPOUT1 = pulldown_4_out ? {controlunit_1_p3_2, controlunit_1_p3} : 32'bz;  // Driver driver_2
  PullDown pulldown_4 (.out(pulldown_4_out));
  or or_3 (pulldown_4_out, controlunit_1_p13, controlunit_1_p11[1]);
  PullDown #(.Bits(32)) pulldown_5 (.out(GPOUT1));
  PullDown #(.Bits(32)) pulldown_6 (.out(GPOUT2));

  // Notes on the sheet:
  //   clk: Hz: 50000
  //   contents of eepromdualport_1 (hex, n*v repeats v):
  //   ac200010,d8010000,ace00005,b8070000,bc000000,ada00002,35cd0010,25ce0002,b40b7000,
  //   25ce0001,b40c7000,25ce0001,b40a7000,29ce0003,b40a7000,bc000000,ad40ffff,ad60000f,
  //   ad8000af,ace00005,b8070000,ade00000,ac200019,c40f0800,ad200022,ad00001c,c8080000,
  //   d8090000,25ef0001,256b0001,ace00005,b8070000,ac600016,d8030000
endmodule
